// Logisim project logisim_evo_2bit_counter.circ as structural Verilog: 1 circuit, main circuit main
module main (
);

  wire clock_1_out, d_ff_2_qn, xor_1_out;
  wire [1:0] d_ff_2_q;

  Clock clock_1 (.out(clock_1_out));
  xor xor_1 (xor_1_out, d_ff_2_q[1], d_ff_2_q[0]);
  D_Flip_Flop d_ff_1 (.D(xor_1_out), .clk(clock_1_out), .Q(d_ff_2_q[1]));  // open: Qn, preset, reset
  D_Flip_Flop d_ff_2 (.D(d_ff_2_qn), .clk(clock_1_out), .Q(d_ff_2_q[0]), .Qn(d_ff_2_qn));  // open: preset, reset
  Hex_Digit_Display hex_digit_display_1 (.value({2'b00, d_ff_2_q}));  // open: dp
endmodule
