// Logisim project logisim_evo_4bit_adder.circ as structural Verilog: 1 circuit, main circuit main
module main (
);

  wire adder_1_cout, adder_2_cout, adder_3_cout, IN_A_sw1, IN_A_sw2, IN_A_sw3, IN_A_sw4, IN_B_sw1, IN_B_sw2,
       IN_B_sw3, IN_B_sw4;
  wire [3:0] A_out, adder_1_out, adder_5_out, B_out;

  DipSwitch #(.number(4)) IN_B (.sw1(IN_B_sw1), .sw2(IN_B_sw2), .sw3(IN_B_sw3), .sw4(IN_B_sw4));
  DipSwitch #(.number(4)) IN_A (.sw1(IN_A_sw1), .sw2(IN_A_sw2), .sw3(IN_A_sw3), .sw4(IN_A_sw4));
  Slider #(.width(4)) A (.out(A_out));
  Slider #(.width(4)) B (.out(B_out));
  Adder #(.width(1)) adder_1 (.a(IN_B_sw1), .b(IN_A_sw1), .out(adder_1_out[0]), .cout(adder_1_cout));  // open: cin
  Adder #(.width(1)) adder_2 (
    .a(IN_B_sw2), .b(IN_A_sw2), .out(adder_1_out[1]), .cin(adder_1_cout), .cout(adder_2_cout));
  Adder #(.width(1)) adder_3 (
    .a(IN_B_sw3), .b(IN_A_sw3), .out(adder_1_out[2]), .cin(adder_2_cout), .cout(adder_3_cout));
  Adder #(.width(1)) adder_4 (.a(IN_B_sw4), .b(IN_A_sw4), .out(adder_1_out[3]), .cin(adder_3_cout));  // open: cout
  Adder #(.width(4)) adder_5 (.a(A_out), .b(B_out), .out(adder_5_out));  // open: cin, cout
  Hex_Digit_Display hex_digit_display_1 (.value(adder_1_out));  // open: dp
  Hex_Digit_Display hex_digit_display_2 (.value(adder_5_out));  // open: dp
endmodule
