// Logisim project logisim_evo_4bit_register.circ as structural Verilog: 1 circuit, main circuit main
module main (
);

  wire clock_1_out;
  wire [3:0] A_out, d_ff_1_q;

  Slider #(.width(4)) A (.out(A_out));
  Clock clock_1 (.out(clock_1_out));
  Hex_Digit_Display hex_digit_display_1 (.value(A_out));  // open: dp
  D_Flip_Flop d_ff_1 (.D(A_out[0]), .clk(clock_1_out), .Q(d_ff_1_q[0]));  // open: Qn, preset, reset
  D_Flip_Flop d_ff_2 (.D(A_out[1]), .clk(clock_1_out), .Q(d_ff_1_q[1]));  // open: Qn, preset, reset
  D_Flip_Flop d_ff_3 (.D(A_out[2]), .clk(clock_1_out), .Q(d_ff_1_q[2]));  // open: Qn, preset, reset
  D_Flip_Flop d_ff_4 (.D(A_out[3]), .clk(clock_1_out), .Q(d_ff_1_q[3]));  // open: Qn, preset, reset
  Hex_Digit_Display hex_digit_display_2 (.value(d_ff_1_q));  // open: dp
endmodule
