// Logisim project logisim_evo_latch_vs_flipflop.circ as structural Verilog: 1 circuit, main circuit main
module main (
  input  D,
  output QL,
  output QFF
);

  wire and_1_out, and_2_out, and_3_out, and_4_out, and_5_out, and_6_out, CLK_out, nor_1_out, nor_3_out,
       nor_4_out, nor_6_out, not_1_out, not_2_out, not_3_out, not_4_out;

  Clock CLK (.out(CLK_out));
  not not_1 (not_1_out, CLK_out);
  not not_2 (not_2_out, D);
  not not_3 (not_3_out, D);
  and and_1 (and_1_out, D, CLK_out);
  and and_2 (and_2_out, CLK_out, not_2_out);
  and and_3 (and_3_out, D, not_1_out);
  and and_4 (and_4_out, not_1_out, not_3_out);
  nor nor_1 (nor_1_out, and_1_out, QL);
  nor nor_2 (QL, nor_1_out, and_2_out);
  nor nor_3 (nor_3_out, and_3_out, nor_4_out);
  nor nor_4 (nor_4_out, nor_3_out, and_4_out);
  not not_4 (not_4_out, nor_3_out);
  and and_5 (and_5_out, nor_3_out, CLK_out);
  and and_6 (and_6_out, CLK_out, not_4_out);
  nor nor_5 (QFF, and_5_out, nor_6_out);
  nor nor_6 (nor_6_out, QFF, and_6_out);
endmodule
